# Fritzing sketch sensing (saved by Fritzing 1.0.8)

parts:
  U1 = ESP32S-HiLetgo [part_number=ESP32S-HiLetgo]
  Part1 = Flora GPS
  Part2 = InvenSense MPU6050
  R1 = Photocell (LDR) [power=0.25W dark_resistance_@0.01lx=300kΩ light_resistance_@100lx=400Ω luminance=10lx package=THT]
  R2 = Resistor [tolerance=±5% power=0.25W resistance=4.7k package=THT]

nets:
  3.3V: U1.3.3, Part1.3.3V, Part2.VCC, R1.pin_0
  N1: U1.GPIO34, R1.pin_1
  GND: U1.GND, Part1.GND, Part2.GND, R2.Pin_1
  N2: U1.GPIO16, Part1.TX
  N3: U1.GPIO17, Part1.RX
  N4: U1.GPIO21, Part2.SDA
  N5: U1.GPIO22, Part2.SCL

custom parts:
  ESP32S-HiLetgo: HiLetgo ESP-WROOM-32 ESP32 ESP-32S Development Board 2.4GHz Dual-Mode WiFi + Bluetooth Dual Cores Microcontroller The ESP32 integrated with Antenna switches, RF Balun, power amplifiers, low-noise amplifiers, filters, and management modules, and the entire solution occupies the least area of PCB. 2.4 GHz Wi-Fi plus Bluetooth dual-mode chip, with TSMC Ultra-low power consumption 40nm technology,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
